# Fritzing sketch v3 (saved by Fritzing 0.9.3b)

parts:
  IC1 = MCP23017 I2C I/O Expander
  LED2 = LED - 3mm [color="Green (560nm)" package="3 mm [THT]"]  # not connected
  LED3 = LED - 3mm [color="Red (633nm)" package="3 mm [THT]"]  # not connected
  LED4 = LED - 3mm [color="Green (560nm)" package="3 mm [THT]"]  # not connected
  LED5 = LED - 3mm [color="Red (633nm)" package="3 mm [THT]"]  # not connected
  LED6 = LED - 3mm [color="Green (560nm)" package="3 mm [THT]"]  # not connected
  LED7 = LED - 3mm [color="Red (633nm)" package="3 mm [THT]"]  # not connected
  LED8 = LED - 3mm [color="Green (565nm)" package="3 mm [THT]"]  # not connected
  R2 = Resistor [tolerance=±5% resistance=220 package=THT]
  R3 = Resistor [tolerance=±5% resistance=220 package=THT]
  R4 = Resistor [tolerance=±5% resistance=220 package=THT]
  R5 = Resistor [tolerance=±5% resistance=220 package=THT]
  R6 = Resistor [tolerance=±5% resistance=220 package=THT]
  R7 = Resistor [tolerance=±5% resistance=220 package=THT]
  R8 = Resistor [tolerance=±5% resistance=220 package=THT]
  R1 = Resistor [tolerance=±5% resistance=220 package=THT]
  R9 = Resistor [tolerance=±5% resistance=220 package=THT]
  R10 = Resistor [tolerance=±5% resistance=220 package=THT]
  R11 = Resistor [tolerance=±5% resistance=220 package=THT]
  R12 = Resistor [tolerance=±5% resistance=220 package=THT]
  R13 = Resistor [tolerance=±5% resistance=220 package=THT]
  R14 = Resistor [tolerance=±5% resistance=220 package=THT]
  R15 = Resistor [tolerance=±5% resistance=220 package=THT]
  R16 = Resistor [tolerance=±5% resistance=220 package=THT]
  LED9 = LED - 3mm [color="Green (560nm)" package="3 mm [THT]"]  # not connected
  LED11 = LED - 3mm [color="Red (633nm)" package="3 mm [THT]"]
  LED12 = LED - 3mm [color="Red (633nm)" package="3 mm [THT]"]  # not connected
  LED13 = LED - 3mm [color="Red (633nm)" package="3 mm [THT]"]  # not connected
  LED14 = LED - 3mm [color="Green (560nm)" package="3 mm [THT]"]  # not connected
  LED15 = LED - 3mm [color="Red (633nm)" package="3 mm [THT]"]  # not connected
  LED16 = LED - 3mm [color="Green (560nm)" package="3 mm [THT]"]  # not connected
  WeMos_D1_Mini1 = WeMos D1 Mini
  Part1 = MPR121 Breakout
  LED1 = LED - 3mm [color="Red (633nm)" package="3 mm [THT]"]
  LED17 = LED - 3mm [color="Green (560nm)" package="3 mm [THT]"]
  U1 = TOUCH [package=touch1]
  U2 = TOUCH [package=touch1]
  U3 = TOUCH [package=touch1]
  U4 = TOUCH [package=touch1]
  U5 = TOUCH [package=touch1]
  U6 = TOUCH [package=touch1]
  U7 = TOUCH [package=touch1]
  U8 = TOUCH [package=touch1]

nets:
  N1: IC1.GPB0, R10.Pin_0
  N2: IC1.GPB1, R15.Pin_0
  N3: IC1.GPB2, R13.Pin_0
  N4: IC1.GPB3, R11.Pin_0
  N5: IC1.GPB4, R14.Pin_0
  N6: IC1.GPB5, R12.Pin_0
  N7: IC1.GPB6, R9.Pin_0
  N8: IC1.GPB7, R16.Pin_0
  VDD: IC1.VDD, WeMos_D1_Mini1.3V3, Part1.3.3V
  VSS: IC1.VSS, LED11.cathode, Part1.GND, LED17.cathode
  N9: IC1.SCL, WeMos_D1_Mini1.D4, Part1.SCL
  N10: IC1.SDA, WeMos_D1_Mini1.D3, Part1.SDA
  N11: IC1.GPA0, R8.Pin_1
  N12: IC1.GPA1, R7.Pin_1
  N13: IC1.GPA2, R6.Pin_1
  N14: IC1.GPA3, R5.Pin_1
  N15: IC1.GPA4, R4.Pin_1
  N16: IC1.GPA5, R3.Pin_1
  N17: IC1.GPA6, R2.Pin_1
  N18: IC1.GPA7, R1.Pin_1
  N19: WeMos_D1_Mini1.G, LED1.cathode
  N20: Part1.ELE7, U1.T2
  N21: Part1.ELE6, U2.T2
  N22: Part1.ELE5, U3.T2
  N23: Part1.ELE4, U4.T2
  N24: Part1.ELE3, U5.T2
  N25: Part1.ELE2, U6.T2
  N26: Part1.ELE1, U7.T2
  N27: Part1.ELE0, U8.T2

custom parts:
  MCP23017 I2C I/O Expander: The MCP23017 uses two i2c pins (these can be shared with other i2c devices), and in exchange gives you 16 general purpose pins. You can set each of 16 pins to be input, output, input with a pullup or open drain. There's even the ability to get an interrupt via an external pin when any of the inputs change so you don't have to keep polling the chip.
  TOUCH: Electrode for resistive touch detection
