# Fritzing sketch v4 (saved by Fritzing 0.9.3b)

parts:
  WeMos_D1_Mini1 = WeMos D1 Mini
  Part1 = 16-Channel 12-bit PWM Servo Driver - I2C [part_number=815]
  J1 = Basic Servo
  S1 = Taiway 100-SP-X-T1 SPDT Miniature Toggle Switch [part_number=100-SP-X-T1-0-0-B1-M2 package=THT]
  S2 = Taiway 100-SP-X-T1 SPDT Miniature Toggle Switch [part_number=100-SP-X-T1-0-0-B1-M2 package=THT]
  J2 = Basic Servo
  J3 = Basic Servo
  J4 = Basic Servo

nets:
  VCC: WeMos_D1_Mini1.3V3, Part1.5.0V, J1.vcc, J2.vcc, J3.vcc, J4.vcc
  N1: WeMos_D1_Mini1.5V, Part1.PWRIN
  N2: WeMos_D1_Mini1.D3, Part1.SCL
  N3: WeMos_D1_Mini1.D4, Part1.VCC, Part1.SDA
  N4: WeMos_D1_Mini1.D5, S1.L1
  N5: WeMos_D1_Mini1.D6, S1.COM, S2.COM
  N6: WeMos_D1_Mini1.D7, S2.L1
  GND: WeMos_D1_Mini1.G, Part1.GND, Part1.OE, J1.gnd, J2.gnd, J3.gnd, J4.gnd
  N7: Part1.PWM3, J4.pulse
  N8: Part1.PWM2, J3.pulse
  N9: Part1.PWM1, J2.pulse
  N10: Part1.PWM0, J1.pulse

custom parts:
  16-Channel 12-bit PWM Servo Driver - I2C: You want to make a cool robot, maybe a hexapod walker, or maybe just a piece of art with a lot of moving parts. Or maybe you want to drive a lot of LEDs with precise PWM output. Using only two pins, control 16 free-running PWM outputs! You can even chain up 62 breakouts to control up to 992 PWM outputs.
